# Fritzing sketch light-up-alarm-clock-hardware-diagram (saved by Fritzing 0.9.3b)
breadboards: 1

parts:
  Raspberry_Pi_1 = Raspberry Pi 3 [part_number=RPI-3-V1.2]
  R1 = Resistor [tolerance=±5% resistance=220 package=THT]
  Q1 = NPN-Transistor [package="TO92 [THT]"]
  LED1 = LEDs [package=led10mm]
  LED9 = LEDs [package=led10mm]
  LED2 = LEDs [package=led10mm]
  LED10 = LEDs [package=led10mm]
  LED3 = LEDs [package=led10mm]
  LED4 = LEDs [package=led10mm]
  LED7 = LEDs [package=led10mm]
  LED8 = LEDs [package=led10mm]
  LED5 = LEDs [package=led10mm]
  LED6 = LEDs [package=led10mm]

nets:
  N1: Raspberry_Pi_1.GND, Q1.E
  N2: Raspberry_Pi_1.GPIO17, R1.Pin_1
  N3: Raspberry_Pi_1.5V, LED1.C, LED9.C, LED2.C, LED10.C, LED3.C, LED4.C, LED7.C, LED8.C, LED5.C, LED6.C
  N4: R1.Pin_0, Q1.B
  N5: Q1.C, LED1.A, LED9.A, LED2.A, LED10.A, LED3.A, LED4.A, LED7.A, LED8.A, LED5.A, LED6.A
